# Fritzing sketch GUI-app (saved by Fritzing 0.9.3b)
breadboards: 1

parts:
  Raspberry_Pi_1 = Raspberry Pi 3 [part_number=RPI-3-V1.2]
  Servo_Battery_5v = 4 x AAA Battery Mount
  Fan_Battery = Battery block 9V
  M1 = Dagu DGServo 9g (Top view) [part_number=RS001B]
  LED1 = LED - 5mm [color="Red (633nm)" package="5 mm [THT]"]
  SPKR1 = Loudspeaker  # not connected
  U1 = 2-Channel 5v Relay Shield [package=relay-2ch5v10a]
  F1 = Fan - 4 wire [package=THT]

nets:
  N1: Raspberry_Pi_1.GPIO3, F1.PWM
  N2: Raspberry_Pi_1.GPIO4, LED1.anode
  GND: Raspberry_Pi_1.GND, Servo_Battery_5v.-, Fan_Battery.-, M1.gnd, LED1.cathode, F1.GND
  N3: Raspberry_Pi_1.GPIO17, M1.pulse
  N4: Raspberry_Pi_1.GPIO27, U1.IN1
  N5: Fan_Battery.+, F1.Power

custom parts:
  2-Channel 5v Relay Shield: 2 Channel 5v Relay Shield w. 2x SPD-06VDC-SD-C
  Fan - 4 wire: Fan, 4 wire with tach.
